// Logisim project Test.circ as structural Verilog: 1 circuit, main circuit main
module main (
);

  wire clock_1_out, clock_2_out, lvc573_1_p2, lvc573_1_p6, lvc16373_1_p2, lvc16373_1_p9, lvc16373_1_p10;
  wire [3:0] counter_1_q, counter_2_q;

  Clock clock_1 (.out(clock_1_out));
  Clock clock_2 (.out(clock_2_out));
  Random random_1 ();  // open: clk, next, out, clr
  Counter #(.max('hf), .width(4)) counter_1 (
    .Q(counter_1_q), .clk(clock_1_out));  // open: load, D, count, carry, up, clr
  Random random_2 ();  // open: clk, next, out, clr
  Counter #(.max('hf), .width(4)) counter_2 (
    .Q(counter_2_q), .clk(clock_2_out));  // open: load, D, count, carry, up, clr
  // LVC4245 lvc4245_1: pin names not known
  // DS1813 ds1813_1: pin names not known
  // LVC16373 lvc16373_1: pin names not known; wires that end beside it: clock_1_out, lvc16373_1_p2, counter_1_q[0], lvc16373_1_p2, counter_1_q[2], counter_1_q[1], lvc16373_1_p2, counter_1_q[3], lvc16373_1_p9, lvc16373_1_p10
  // LVC573 lvc573_1: pin names not known; wires that end beside it: clock_2_out, lvc573_1_p2, counter_2_q[0], lvc573_1_p2, counter_2_q[2], lvc573_1_p6
  // LVC543 lvc543_1: pin names not known
  // Probe on lvc16373_1_p9
  // Probe on lvc16373_1_p10
  // Probe on lvc573_1_p6
  // W65C816 w65c816_1: pin names not known
  // W65C02S w65c02s_1: pin names not known
endmodule
