// Logisim project demo.circ as structural Verilog: 1 circuit, main circuit main
module main (
);

  wire Abort_816_out, and_1_out, clock_1_out, IRQ_816_out, NMI_816_out, not_1_out, not_2_out, not_3_out,
       not_4_out, not_5_out, not_6_out, pull_resistor_2_node, Reset_816_out, w65c816s_1_p1, w65c816s_1_p2,
       w65c816s_1_p3, w65c816s_1_p15, w65c816s_1_p16, w65c816s_1_p17, w65c816s_1_p18, w65c816s_1_p19,
       w65c816s_1_p20;
  wire [7:0] w65c816s_1_p13, w65c816s_1_p14;
  wire [15:0] w65c816s_1_p12;

  Clock clock_1 (.out(clock_1_out));
  Button Abort_816 (.out(Abort_816_out));
  Button IRQ_816 (.out(IRQ_816_out));
  Button NMI_816 (.out(NMI_816_out));
  Button Reset_816 (.out(Reset_816_out));
  not not_1 (not_1_out, Abort_816_out);
  not not_2 (not_2_out, IRQ_816_out);
  not not_3 (not_3_out, NMI_816_out);
  not not_4 (not_4_out, Reset_816_out);
  // W65C816S w65c816s_1: pin names not known; wires that end beside it: w65c816s_1_p1, w65c816s_1_p2, w65c816s_1_p3, not_1_out, not_2_out, not_3_out, not_4_out, clock_1_out, w65c816s_1_p1, w65c816s_1_p2, w65c816s_1_p3, w65c816s_1_p12, w65c816s_1_p13, w65c816s_1_p14, w65c816s_1_p15, w65c816s_1_p16, w65c816s_1_p17, w65c816s_1_p18, w65c816s_1_p19, w65c816s_1_p20, w65c816s_1_p17, w65c816s_1_p18, w65c816s_1_p19, w65c816s_1_p20
  Register #(.trigger("high")) register_1 (.D(w65c816s_1_p13), .clk(clock_1_out));  // open: en, Q, clr
  // Probe on w65c816s_1_p14
  Pull_Resistor #(.pull(1)) pull_resistor_1 (.node(w65c816s_1_p16));
  not not_5 (not_5_out, clock_1_out);
  not not_6 (not_6_out, w65c816s_1_p15);
  and and_1 (and_1_out, not_5_out, w65c816s_1_p15);
  Pull_Resistor #(.pull(1)) pull_resistor_2 (.node(pull_resistor_2_node));
  // Probe on w65c816s_1_p12
  RAM #(.addrWidth(16), .databus("bidir"), .enables("line"), .trigger("high"), .\type ("nonvolatile")) ram_1 (
    .addr(w65c816s_1_p12), .data(w65c816s_1_p14));  // open: we, oe, clk
  // Probe on w65c816s_1_p14
endmodule
